# Fritzing sketch Layout (saved by Fritzing 0.9.3b)
breadboards: 1

parts:
  Bauteil1 = Arduino Nano (Rev3.0)
  RGB_SMD_LED1 = SMD RGB LED (WS2812) [package=5050]

nets:
  GND: Bauteil1.GND, RGB_SMD_LED1.VSS
  N1: Bauteil1.D3, RGB_SMD_LED1.DIn
  5V: Bauteil1.5V, RGB_SMD_LED1.VCC
